# Fritzing sketch radiator (saved by Fritzing 0.9.10b)
breadboards: 1

parts:
  JACK1 = 2.1mm Barrel Jack with Terminal Block
  U1 = Mini-360 DC-DC Buck converter [package=THT]
  Part1 = Arduino Nano (Rev3.0)
  Pololu_A1 = Pololu A4988 [package=SO16]
  M1 = Stepper Motor - Bipolar

nets:
  N1: JACK1.POS, U1.IN+, Pololu_A1.VMOT
  N2: JACK1.NEG, U1.IN-, Pololu_A1.GND#14
  VIN: U1.OUT+, Part1.VIN, Pololu_A1.VDD
  N3: U1.OUT-, Part1.GND, Pololu_A1.GND#8
  N4: Part1.D2, Pololu_A1.DIR
  N5: Part1.D3, Pololu_A1.STEP
  N6: Pololu_A1.RESET, Pololu_A1.SLEEP
  N7: Pololu_A1.1B, M1.B
  N8: Pololu_A1.1A, M1.A
  N9: Pololu_A1.2A, M1.C
  N10: Pololu_A1.2B, M1.D

custom parts:
  Mini-360 DC-DC Buck converter: Mini-360 DC-DC Buck converter. Tiny buck step down voltage converter, input voltage 4.75 to 23V output 1 to 17V adjustable. Available from ebay and the like.
